// Logisim project 4X3 memory.circ as structural Verilog: 1 circuit, main circuit main
module main (
  input  Bit2,
  input  Bit1,
  input  Bit0,
  input  Reset,
  input  S1,
  input  S0,
  input  nWE,
  output Bit2_2,
  output Bit1_2,
  output Bit0_2
);

  wire and_1_out, and_2_out, and_3_out, and_4_out, and_5_out, and_6_out, and_7_out, and_8_out, and_9_out,
       and_10_out, and_11_out, and_12_out, and_13_out, and_14_out, and_15_out, and_16_out, and_17_out,
       and_18_out, and_19_out, and_20_out, and_21_out, and_22_out, clock_1_out, d_ff_1_q, d_ff_2_q, d_ff_3_q,
       d_ff_4_q, d_ff_5_q, d_ff_6_q, d_ff_7_q, d_ff_8_q, d_ff_9_q, d_ff_10_q, d_ff_11_q, d_ff_12_q,
       not_1_out, not_2_out, not_3_out, not_4_out, not_5_out, or_1_out, or_2_out, or_3_out;

  Clock clock_1 (.out(clock_1_out));
  and and_1 (and_1_out, and_2_out, and_7_out);
  and and_2 (and_2_out, clock_1_out, nWE);
  D_Flip_Flop d_ff_1 (.clk(and_1_out), .D(Bit2), .Q(d_ff_1_q), .reset(Reset));  // open: Qn, preset, en
  D_Flip_Flop d_ff_2 (.clk(and_1_out), .D(Bit1), .Q(d_ff_2_q), .reset(Reset));  // open: Qn, preset, en
  D_Flip_Flop d_ff_3 (.clk(and_1_out), .D(Bit0), .Q(d_ff_3_q), .reset(Reset));  // open: Qn, preset, en
  and and_3 (and_3_out, d_ff_1_q, and_7_out);
  and and_4 (and_4_out, d_ff_2_q, and_7_out);
  and and_5 (and_5_out, d_ff_3_q, and_7_out);
  and and_6 (and_6_out, and_2_out, and_12_out);
  and and_7 (and_7_out, not_2_out, not_1_out);
  not not_1 (not_1_out, S0);
  not not_2 (not_2_out, S1);
  D_Flip_Flop d_ff_4 (.clk(and_6_out), .D(Bit2), .Q(d_ff_4_q), .reset(Reset));  // open: Qn, preset, en
  D_Flip_Flop d_ff_5 (.clk(and_6_out), .D(Bit1), .Q(d_ff_5_q), .reset(Reset));  // open: Qn, preset, en
  D_Flip_Flop d_ff_6 (.clk(and_6_out), .D(Bit0), .Q(d_ff_6_q), .reset(Reset));  // open: Qn, preset, en
  and and_8 (and_8_out, d_ff_4_q, and_12_out);
  and and_9 (and_9_out, d_ff_5_q, and_12_out);
  and and_10 (and_10_out, d_ff_6_q, and_12_out);
  and and_11 (and_11_out, and_2_out, and_16_out);
  and and_12 (and_12_out, not_3_out, S0);
  not not_3 (not_3_out, S1);
  D_Flip_Flop d_ff_7 (.clk(and_11_out), .D(Bit2), .Q(d_ff_7_q), .reset(Reset));  // open: Qn, preset, en
  D_Flip_Flop d_ff_8 (.clk(and_11_out), .D(Bit1), .Q(d_ff_8_q), .reset(Reset));  // open: Qn, preset, en
  D_Flip_Flop d_ff_9 (.clk(and_11_out), .D(Bit0), .Q(d_ff_9_q), .reset(Reset));  // open: Qn, preset, en
  and and_13 (and_13_out, d_ff_7_q, and_16_out);
  and and_14 (and_14_out, d_ff_8_q, and_16_out);
  and and_15 (and_15_out, d_ff_9_q, and_16_out);
  and and_16 (and_16_out, S1, not_4_out);
  not not_4 (not_4_out, S0);
  D_Flip_Flop d_ff_10 (.clk(and_17_out), .D(Bit2), .Q(d_ff_10_q), .reset(Reset));  // open: Qn, preset, en
  D_Flip_Flop d_ff_11 (.clk(and_17_out), .D(Bit1), .Q(d_ff_11_q), .reset(Reset));  // open: Qn, preset, en
  and and_17 (and_17_out, and_2_out, and_18_out);
  and and_18 (and_18_out, S0, S1);
  D_Flip_Flop d_ff_12 (.clk(and_17_out), .D(Bit0), .Q(d_ff_12_q), .reset(Reset));  // open: Qn, preset, en
  and and_19 (and_19_out, d_ff_10_q, and_18_out);
  and and_20 (and_20_out, d_ff_11_q, and_18_out);
  and and_21 (and_21_out, d_ff_12_q, and_18_out);
  or or_1 (or_1_out, and_3_out, and_8_out, and_13_out, and_19_out);
  or or_2 (or_2_out, and_4_out, and_9_out, and_14_out, and_20_out);
  or or_3 (or_3_out, and_5_out, and_10_out, and_15_out, and_21_out);
  and and_22 (and_22_out, clock_1_out, not_5_out);
  not not_5 (not_5_out, nWE);
  and and_23 (Bit2_2, or_1_out, and_22_out);
  and and_24 (Bit1_2, or_2_out, and_22_out);
  and and_25 (Bit0_2, and_22_out, or_3_out);

  // Notes on the sheet:
  //   Word 0
  //   Word0 select
  //   Word 1
  //   Word1 select
  //   Word 2
  //   Word2 select
  //   Word 3
  //   Word3 select
endmodule
