// Logisim project Excersise.circ as structural Verilog: 1 circuit, main circuit main
module main (
  output out_1,
  output out_2,
  output out_3
);

  wire clock_1_out, Q0_q, Q0_qn, Q2_q, Q2_qn, Q3_qn;

  Clock clock_1 (.out(clock_1_out));
  D_Flip_Flop Q0 (.clk(clock_1_out), .D(Q0_qn), .Q(Q0_q), .Qn(Q0_qn));  // open: preset, en, reset
  D_Flip_Flop Q2 (.clk(Q0_q), .D(Q2_qn), .Q(Q2_q), .Qn(Q2_qn));  // open: preset, en, reset
  D_Flip_Flop Q3 (.clk(Q2_q), .D(Q3_qn), .Q(out_3), .Qn(Q3_qn));  // open: preset, en, reset
endmodule
