// Logisim project HW#5Q1.circ as structural Verilog: 1 circuit, main circuit main
module main (
  input  x,
  input  y,
  input  z,
  output S,
  output C
);

  wire and_1_out, and_2_out, xor_1_out;

  xor xor_1 (xor_1_out, x, y);
  and and_1 (and_1_out, xor_1_out, z);
  and and_2 (and_2_out, x, y);
  xor xor_2 (S, xor_1_out, z);
  or or_1 (C, and_1_out, and_2_out);
endmodule
