// Logisim project HW#5Q2.circ as structural Verilog: 1 circuit, main circuit main
module main (
  input  x,
  input  y,
  output S,
  output Q,
  output Carry_out
);

  wire adder_1_cout, Clock_out;

  not not_1 (Carry_out, adder_1_cout);
  Adder #(.width(1)) adder_1 (.a(x), .b(y), .out(S), .cin(Q), .cout(adder_1_cout));
  D_Flip_Flop d_ff_1 (.clk(Clock_out), .D(Carry_out), .Q(Q));  // open: Qn, preset, en, reset
  Clock Clock (.out(Clock_out));

  // Notes on the sheet:
  //   Carry in
  //   Sum
endmodule
