// Logisim project HW#5Q3.circ as structural Verilog: 1 circuit, main circuit main
module main (
  input  x,
  input  y,
  output z,
  output A,
  output B
);

  wire B_ny_out, By_out, clock_1_out, not_1_out, not_2_out, nxy_2_out, nxy_out, nyA_out, or_1_out, or_2_out,
       or_3_out, xB_out, xy_out;

  not not_1 (not_1_out, x);
  not not_2 (not_2_out, y);
  and nxy (nxy_out, not_1_out, y);
  and By (By_out, y, B);
  and B_ny (B_ny_out, B, not_2_out);
  and xy (xy_out, y, x);
  and xB (xB_out, x, B);
  and nyA (nyA_out, not_2_out, A);
  and nxy_2 (nxy_2_out, not_1_out, y);
  or or_1 (or_1_out, nxy_out, By_out);
  or or_2 (or_2_out, B_ny_out, xy_out);
  or or_3 (or_3_out, xB_out, nyA_out);
  or x_nxy (z, x, nxy_2_out);
  Clock clock_1 (.out(clock_1_out));
  D_Flip_Flop d_ff_1 (.clk(clock_1_out), .D(or_1_out), .Q(A));  // open: Qn, preset, en, reset
  J_K_Flip_Flop j_k_ff_1 (.J(or_2_out), .clk(clock_1_out), .K(or_3_out), .Q(B));  // open: Qn, preset, en, reset
endmodule
