// Logisim project HW#5Q4.circ as structural Verilog: 1 circuit, main circuit main
module main (
  output A,
  output B,
  output C
);

  wire and_1_out, and_2_out, clock_1_out, j_k_ff_1_qn, j_k_ff_2_qn, j_k_ff_3_qn, or_1_out, or_2_out,
       or_3_out, or_4_out;

  or or_1 (or_1_out, C, B);
  or or_2 (or_2_out, j_k_ff_1_qn, j_k_ff_3_qn);
  and and_1 (and_1_out, j_k_ff_2_qn, j_k_ff_1_qn);
  or or_3 (or_3_out, j_k_ff_3_qn, B);
  and and_2 (and_2_out, B, A);
  Clock clock_1 (.out(clock_1_out));
  or or_4 (or_4_out, and_1_out, and_2_out);
  J_K_Flip_Flop j_k_ff_1 (
    .J(or_3_out), .clk(clock_1_out), .K(or_1_out), .Q(A), .Qn(j_k_ff_1_qn));  // open: preset, en, reset
  J_K_Flip_Flop j_k_ff_2 (
    .J(or_2_out), .clk(clock_1_out), .K(or_2_out), .Q(B), .Qn(j_k_ff_2_qn));  // open: preset, en, reset
  J_K_Flip_Flop j_k_ff_3 (.J(or_4_out), .clk(clock_1_out), .Q(C), .Qn(j_k_ff_3_qn));  // open: K, preset, en, reset
endmodule
