// Logisim project HW-Q2-Implementation.circ as structural Verilog: 1 circuit, main circuit main
module main (
  input  X,
  input  Y,
  output S,
  output Q,
  output Carry_Out
);

  wire adder_1_cout, clock_1_out;

  not not_1 (Carry_Out, adder_1_cout);
  Adder #(.width(1)) adder_1 (.a(X), .b(Y), .out(S), .cin(Q), .cout(adder_1_cout));
  Clock clock_1 (.out(clock_1_out));
  D_Flip_Flop d_ff_1 (.clk(clock_1_out), .D(Carry_Out), .Q(Q));  // open: Qn, preset, en, reset

  // Notes on the sheet:
  //   Carry In
  //   Clock
endmodule
