// Logisim project HW5-Q1.circ as structural Verilog: 1 circuit, main circuit main
module main (
  input  X,
  input  Y,
  input  Z,
  output C,
  output S
);

  wire XY_out, XZ_out, Y_XOR_Z_out, YZ_out;

  and XY (XY_out, X, Y);
  and XZ (XZ_out, X, Z);
  xor Y_XOR_Z (Y_XOR_Z_out, Y, Z);
  and YZ (YZ_out, Y, Z);
  xor X_XOR_Y_XOR_Z (S, X, Y_XOR_Z_out);
  or XY_XZ_YZ (C, XY_out, YZ_out, XZ_out);
endmodule
