// Logisim project HW5Q4P4.circ as structural Verilog: 2 circuits, main circuit main
module main (
);

  wire A_q, A_qn, AB_out, B_C_out, B_qn, C_q, C_qn, nA_nB_out, nA_nC_out, nB_nC_out, or_1_out;

  or nB_nC (nB_nC_out, A_q, B_qn);
  and nA_nB (nA_nB_out, A_qn, C_qn);
  and AB (AB_out, A_q, A_q);
  or nA_nC (nA_nC_out, A_qn, B_qn);
  or or_1 (or_1_out, nA_nB_out, AB_out);
  or B_C (B_C_out, A_q, C_q);
  J_K_Flip_Flop A (.J(nB_nC_out), .K(nA_nC_out), .Q(A_q), .Qn(A_qn));  // open: clk, preset, en, reset
  J_K_Flip_Flop B (.J(nA_nC_out), .clk(nA_nC_out), .K(nA_nC_out), .Q(A_q), .Qn(B_qn));  // open: preset, en, reset
  J_K_Flip_Flop C (.J(or_1_out), .clk(nA_nC_out), .K(A_q), .Q(C_q), .Qn(C_qn));  // open: preset, en, reset
endmodule

module HW5Q4 (
);

  wire A_q, C_q, not_1_out, not_2_out, or_1_out, or_2_out, or_3_out;

  buf or_1 (or_1_out, not_2_out);  // OR_Gate
  buf or_2 (or_2_out, C_q);  // OR_Gate
  or or_3 (or_3_out, not_1_out, not_2_out);
  // XOR_Gate xor_1 has open pins: in4=A_q, out=open
  J_K_Flip_Flop A (.J(or_1_out), .K(or_2_out), .Q(A_q));  // open: clk, Qn, preset, en, reset
  J_K_Flip_Flop B (.J(or_3_out), .clk(or_3_out), .K(or_3_out));  // open: Q, Qn, preset, en, reset
  J_K_Flip_Flop C (.Q(C_q));  // open: J, clk, K, Qn, preset, en, reset
  // NOT_Gate not_1 has open pins: in=open, out=not_1_out
  not not_2 (not_2_out, C_q);
endmodule
